# Fritzing sketch Circuit (saved by Fritzing 0.9.2b)
breadboards: 1

parts:
  Part1 = Arduino Uno (Rev3)
  T1 = TMP36 Temperature Sensor [package="TO92 [THT]"]
  R1 = Resistor [tolerance=±5% resistance=1k package="1206 [SMD]"]
  R2 = Photocell (LDR) [package=THT]
  R3 = Resistor [tolerance=±5% resistance=1k package="2010 [SMD]"]
  Part2 = Humidity Temperature Sensor SHT15  # not connected
  LCD1 = LCD screen  # not connected

nets:
  N1: Part1.A4/SDA, R2.pin_1, R3.Pin_1
  N2: Part1.A5/SCL, R1.Pin_0
  GND: Part1.GND, T1.GND, R3.Pin_0
  N3: Part1.5V, T1.+Vs, R2.pin_0
  N4: T1.Vout, R1.Pin_1
